# Fritzing sketch Project2-Pushbutton-Servo (saved by Fritzing 0.9.3b)
breadboards: 1

parts:
  Raspberry_Pi_1 = Raspberry Pi 3 [part_number=RPI-3-V1.2]
  S1 = Pushbutton [package="[THT]"]
  J1 = Basic Servo

nets:
  N1: Raspberry_Pi_1.GIPO27, S1.Pin_3, S1.Pin_4
  N2: Raspberry_Pi_1.GIPO22, J1.pulse
  GND: Raspberry_Pi_1.GND, S1.Pin_1, S1.Pin_2, J1.gnd
  5V: Raspberry_Pi_1.5V, J1.vcc
